# Fritzing sketch Projekt DIVERA247-Monitor-HidSensor_schematic (saved by Fritzing 1.0.2b)

parts:
  LED1 = Super Flux LED blue [color=Blue current=0.030A]
  S1 = SWITCH-MOMENTARY-2 [package=tactile-pth]
  B1 = SR602 MINI Motion Sensor Detector Module
  Bauteil1 = Arduino Pro Micro (Clone)

nets:
  N1: LED1.anode, Bauteil1.D10
  GND: LED1.cathode, S1.2, B1.GND, Bauteil1.GND
  N2: S1.1, Bauteil1.D2
  VCC: B1.VCC, Bauteil1.VCC
  N3: B1.OUT, Bauteil1.D3

custom parts:
  SR602 MINI Motion Sensor Detector Module: Interfacing SR602 PIR Motion Detection Sensor motion sensor
