# Fritzing sketch Projekt DIVERA247-Monitor-HidSensor_schematic_Breadboard (saved by Fritzing 1.0.2b)
breadboards: 1

parts:
  LED1 = Super Flux LED blue [color=Blue current=0.030A]
  S1 = SWITCH-MOMENTARY-2 [package=tactile-pth]
  part = SR602 MINI Motion Sensor Detector Module
  part_2 = Arduino Pro Micro (Clone)

nets:
  N1: LED1.anode, part_2.D10
  GND: LED1.cathode, S1.2, part.GND, part_2.GND
  N2: S1.1, part_2.D2
  VCC: part.VCC, part_2.VCC
  N3: part.OUT, part_2.D3

custom parts:
  SR602 MINI Motion Sensor Detector Module: Interfacing SR602 PIR Motion Detection Sensor motion sensor
